// Logisim project jrmipsprojectGraham.circ as structural Verilog: 20 circuits, main circuit main
module main (
  output [15:0] out_1,
  output [15:0] out_2,
  output [3:0] out_3,
  output [2:0] out_4,
  output [7:0] out_5,
  output [2:0] out_6
);

  wire Addi, Addui, b, bn, bp, branched, bx, bz, Clock, Halt_halt, Imm, J, Jal, Jr, MemRead, MemtoReg,
       MemWrite, multiplexer_2_out, multiplexer_4_out, multiplexer_5_out, not_1_out, not_2_out, Not_Intial,
       putcontrol_1_put, Reset, Sub, Sw, writedecoder_1_writeenable1, writedecoder_1_writeenable2;
  wire [2:0] Operation;
  wire [3:0] multiplexer_6_out_2;
  wire [7:0] multiplexer_11_out, multiplexer_13_out, PC_q, PCpart, ToPC;
  wire [11:0] multiplexer_6_out;
  wire [15:0] Address, ALUOut, ALUOut2, bit_extender_2_out, bit_extender_3_out, ImmTransfer, JrVal,
       multiplexer_1_out, multiplexer_7_out, multiplexer_9_out, PC_1, ram_1_data, rom_1_data, Value,
       WriteData;

  assign PC_1 = {{8{1'b0}}, PCpart};  // Bit_Extender bit_extender_1
  Adder adder_1 (.a(PC_q), .b(8'h1), .out(PCpart), .cin(1'b0));  // open: cout
  Jr_Jal_Control Jr_Jal_Control (.Subop(Sub), .Opcode(out_3), .Jr(Jr), .Jal(Jal));
  AddiControl addicontrol_1 (.SubOp(Sub), .Opcode(out_3), .addi(Addi));
  HaltControl Halt (.SubOp(Sub), .Opcode(out_3), .Halt(Halt_halt));
  Clock clock_1 (.out(Clock));
  Register PC (.D(ToPC), .en(not_1_out), .Q(PC_q), .clk(Clock), .clr(Reset));
  Button u_Reset (.out(Reset));
  AdduiControl adduicontrol_1 (.Subop(Sub), .Opcode(out_3), .addui(Addui));
  not not_1 (not_1_out, Halt_halt);
  Multiplexer #(.width(16), .enable("false")) multiplexer_1 (
    .in0(WriteData), .in1(Value), .out(multiplexer_1_out), .sel(multiplexer_2_out));
  WriteDecoder writedecoder_1 (
    .Opcode(out_3), .Subop(Sub), .WriteEnable1(writedecoder_1_writeenable1),
    .WriteEnable2(writedecoder_1_writeenable2));
  assign bit_extender_2_out = {{8{1'b0}}, out_5};  // Bit_Extender bit_extender_2
  assign bit_extender_3_out = {{8{out_5[7]}}, out_5};  // Bit_Extender bit_extender_3
  Branch Branch (.Opcode(out_3), .b(b));
  PutControl putcontrol_1 (.SubOp(Sub), .Opcode(out_3), .Put(putcontrol_1_put));
  LED led_1 (.in(Halt_halt));
  ALUControl2 alucontrol2_1 (.Subop(Sub), .Opcode(out_3), .Operation(Operation));
  Multiplexer #(.enable("false")) multiplexer_2 (
    .in0(multiplexer_5_out), .in1(1'b1), .out(multiplexer_2_out), .sel(Addi));
  ROM #(.dataWidth(16)) rom_1 (.addr(PC_q), .data(rom_1_data), .sel(1'b1));
  Multiplexer #(.width(16), .enable("false")) multiplexer_3 (
    .in0(bit_extender_2_out), .in1(bit_extender_3_out), .out(ImmTransfer), .sel(not_2_out));
  not not_2 (not_2_out, Sub);
  Multiplexer #(.enable("false")) multiplexer_4 (.in0(Not_Intial), .in1(1'b0), .out(multiplexer_4_out), .sel(Imm));
  Multiplexer #(.enable("false")) multiplexer_5 (.in0(multiplexer_4_out), .in1(1'b1), .out(multiplexer_5_out), .sel(b));
  Register2 register2_1 (
    .WriteInput1(multiplexer_1_out), .WriteInput2(multiplexer_1_out),
    .WriteEnable1(writedecoder_1_writeenable1), .WriteEnable2(writedecoder_1_writeenable2), .Clear(Reset),
    .ReadReg(out_4), .Clock(Clock), .ReadReg2(out_6), .Output(out_2), .Output2(out_1));
  Field Field (.InputData(rom_1_data), .SubOp(Sub), .Immediate(out_5), .RS(out_4), .RT(out_6), .OpCode(out_3));
  Hex_Digit_Display hex_digit_display_1 (.value(multiplexer_6_out_2));  // open: dp
  MemDecoder Mem_Decoder (.Subop(Sub), .Opcode(out_3), .MemWrite(MemWrite), .MemRead(MemRead), .MemToReg(MemtoReg));
  Hex_Digit_Display hex_digit_display_2 (.value(multiplexer_6_out[11:8]));  // open: dp
  Hex_Digit_Display hex_digit_display_3 (.value(multiplexer_6_out[7:4]));  // open: dp
  Multiplexer #(.width(16), .enable("false")) multiplexer_6 (
    .in0({16{1'b0}}), .in1(out_2), .out({multiplexer_6_out_2, multiplexer_6_out}), .sel(putcontrol_1_put));
  Multiplexer #(.width(16), .enable("false")) multiplexer_7 (
    .in0(Value), .in1(ImmTransfer), .out(multiplexer_7_out), .sel(Imm));
  Hex_Digit_Display hex_digit_display_4 (.value(multiplexer_6_out[3:0]));  // open: dp
  Multiplexer #(.width(16), .enable("false")) multiplexer_8 (.in0(out_1), .in1(ImmTransfer), .out(JrVal), .sel(Imm));
  Multiplexer #(.width(16), .enable("false")) multiplexer_9 (
    .in0(out_1), .in1(out_2), .out(multiplexer_9_out), .sel(Sw));
  ImmAndJumpControl Imm_Jump_Control (.Subop(Sub), .Opcode(out_3), .Imm(Imm), .Jump(J));
  Multiplexer #(.width(16), .enable("false")) multiplexer_10 (
    .in0(multiplexer_7_out), .in1(PC_1), .out(WriteData), .sel(Jal));
  ALU alu_1 (.Input_1(out_2), .Input_2(JrVal), .in_3(Operation), .ALU_Output(ALUOut), .Secondary_Output(ALUOut2));
  Multiplexer #(.width(8), .enable("false")) multiplexer_11 (
    .in0(PCpart), .in1(out_5), .out(multiplexer_11_out), .sel(branched));
  BranchDecode Branch_Decoder (
    .A(out_3[3]), .B(out_3[2]), .C(out_3[1]), .D(out_3[0]), .SubOp(Sub), .rs(out_2), .bx(bx), .bz(bz),
    .Branched(branched), .bp(bp), .bn(bn));
  RAM #(.dataWidth(16), .bus("separate")) ram_1 (
    .addr(Address[7:0]), .din(multiplexer_9_out), .data(ram_1_data), .str(MemWrite), .sel(1'b1), .clk(Clock),
    .ld(MemRead), .clr(Reset));
  Multiplexer #(.width(16), .enable("false")) multiplexer_12 (.in0(ALUOut), .in1(out_1), .out(Address), .sel(Sw));
  Multiplexer #(.width(8), .enable("false")) multiplexer_13 (
    .in0(multiplexer_11_out), .in1(out_5), .out(multiplexer_13_out), .sel(J));
  Register #(.width(1)) register_1 (.D(1'b1), .Q(Not_Intial), .clk(Clock), .clr(Reset));  // open: en
  Multiplexer #(.width(8), .enable("false")) multiplexer_14 (
    .in0(multiplexer_13_out), .in1(JrVal[7:0]), .out(ToPC), .sel(Jr));
  Multiplexer #(.width(16), .enable("false")) multiplexer_15 (
    .in0(ALUOut), .in1(ram_1_data), .out(Value), .sel(MemtoReg));
  SwControl swcontrol_1 (.Opcode(out_3), .in_2(Sub), .ALUSrc(Sw));

  // Other names for the same wires on the sheet: Immediate[7:0] = out_5; OPCODE[3:0] = out_3; PutVal[15:0] = out_2;
  //   rs[15:0] = out_2; RS_t[2:0] = out_4; rt[15:0] = out_1; RT_t[2:0] = out_6

  // Notes on the sheet:
  //   Graham Hoehing CS447 Dr.Childers
  //   Project 2 Spring 2017
  //   Do this before new load for correct result
  //   gjh32@pitt.edu
  //   ROM
  //   Bit Extender
  //   contents of rom_1 (hex, n*v repeats v):
  //   8006 8204 2041 b000 b001
  //   LED
  //   ALU
  //   RAM
endmodule

module HaltControl (
  input  SubOp,
  input  [3:0] Opcode,
  output Halt
);

  wire not_1_out;

  not not_1 (not_1_out, Opcode[2]);
  and and_1 (Halt, Opcode[3], not_1_out, Opcode[1], Opcode[0], SubOp);
endmodule

module BranchDecode (
  input  A,
  input  B,
  input  C,
  input  D,
  input  SubOp,
  input  [15:0] rs,
  output bx,
  output bz,
  output Branched,
  output bp,
  output bn
);

  wire comparator_1_eq, comparator_1_gt, comparator_1_lt, not_1_out, not_2_out, not_3_out, not_4_out,
       not_5_out, not_6_out, not_7_out, not_8_out, not_9_out, not_10_out, not_11_out;

  not not_1 (not_1_out, A);
  not not_2 (not_2_out, C);
  not not_3 (not_3_out, comparator_1_eq);
  not not_4 (not_4_out, SubOp);
  not not_5 (not_5_out, A);
  not not_6 (not_6_out, C);
  not not_7 (not_7_out, A);
  not not_8 (not_8_out, D);
  not not_9 (not_9_out, SubOp);
  not not_10 (not_10_out, A);
  not not_11 (not_11_out, D);
  Comparator #(.width(16)) comparator_1 (
    .a(rs), .b({16{1'b0}}), .gt(comparator_1_gt), .eq(comparator_1_eq), .lt(comparator_1_lt));
  and and_1 (bx, not_2_out, not_1_out, B, D, not_4_out, not_3_out);
  and and_2 (bz, not_6_out, not_5_out, B, D, SubOp, comparator_1_eq);
  and and_3 (bp, C, not_7_out, B, not_8_out, not_9_out, comparator_1_gt);
  and and_4 (bn, C, not_10_out, B, not_11_out, SubOp, comparator_1_lt);
  or or_1 (Branched, bx, bz, bp, bn);
endmodule

module ALU (
  input  [15:0] Input_1,
  input  [15:0] Input_2,
  input  [2:0] in_3,
  output [15:0] ALU_Output,
  output [15:0] Secondary_Output
);

  wire [15:0] AddOut, AndOut, divider_1_rem, DivOut, LeftShiftOutV, LiOut, mullOut, multiplier_1_cout,
       NorOut, RightShiftOutV, SubOut;

  Adder #(.width(16)) adder_1 (.a({16{1'b0}}), .b(Input_2), .out(LiOut));  // open: cin, cout
  Adder #(.width(16)) adder_2 (.a(Input_1), .b(Input_2), .out(AddOut));  // open: cin, cout
  Subtractor #(.width(16)) subtractor_1 (.a(Input_1), .b(Input_2), .out(SubOut));  // open: bin, bout
  Multiplier #(.width(16)) multiplier_1 (
    .a(Input_1), .b(Input_2), .out(mullOut), .cout(multiplier_1_cout));  // open: cin
  Divider #(.width(16)) divider_1 (.a(Input_1), .b(Input_2), .out(DivOut), .rem(divider_1_rem));  // open: upper
  assign AndOut = Input_1 & Input_2;  // AND_Gate and_1, 16 bits wide
  assign NorOut = ~(Input_1 | Input_2);  // NOR_Gate nor_1, 16 bits wide
  Shifter #(.width(16)) shifter_1 (.in(Input_1), .\dist (Input_2[3:0]), .out(LeftShiftOutV));
  Shifter #(.width(16), .shift("lr")) shifter_2 (.in(Input_1), .\dist (Input_2[3:0]), .out(RightShiftOutV));
  Multiplexer #(.width(16), .enable("false")) multiplexer_1 (
    .in0(multiplier_1_cout), .in1(divider_1_rem), .out(Secondary_Output), .sel(in_3[0]));
  Multiplexer #(.select(3), .width(16), .enable("false")) multiplexer_2 (
    .in0(AndOut), .in1(NorOut), .in2(AddOut), .in3(SubOut), .in4(DivOut), .in5(mullOut), .in6(LeftShiftOutV),
    .in7(RightShiftOutV), .out(ALU_Output), .sel(in_3));

  // Other names for the same wires on the sheet: input1[15:0] = Input_1; input2[15:0] = Input_2
endmodule

module ImmControl (
  input  [4:0] OP_SubOp,
  output out_2
);

  wire not_1_out, not_2_out, not_3_out;

  not not_1 (not_1_out, OP_SubOp[4]);
  not not_2 (not_2_out, OP_SubOp[3]);
  not not_3 (not_3_out, OP_SubOp[2]);
  and and_1 (out_2, not_1_out, not_3_out, OP_SubOp[1]);

  // Other names for the same wires on the sheet: OP[4:0] = OP_SubOp
endmodule

module PCDecoder (
  input  Op3,
  input  Op2,
  input  Op1,
  input  Op0,
  input  Sub,
  output branch,
  output jump
);

  wire and_1_out, and_2_out, and_3_out, and_4_out, and_5_out, and_6_out, not_1_out;

  and and_1 (and_1_out, Op3, Op0, Sub);
  and and_2 (and_2_out, Op3, Op1, Op0);
  and and_3 (and_3_out, Op3, Op2);
  not not_1 (not_1_out, Sub);
  or or_1 (branch, and_1_out, and_2_out, and_3_out);
  and and_4 (and_4_out, Op3, Op0, not_1_out);
  and and_5 (and_5_out, Op3, Op1);
  and and_6 (and_6_out, Op3, Op2);
  or or_2 (jump, and_4_out, and_5_out, and_6_out);
endmodule

module ALUControl (
  input  [4:0] OP_SubOp,
  output ALUtru
);

  wire and_1_out, and_2_out, and_3_out, and_4_out, and_5_out, not_1_out, not_2_out, not_3_out, not_4_out,
       not_5_out, not_6_out, not_7_out, not_8_out, not_9_out, not_10_out, not_11_out, not_12_out, not_13_out,
       not_14_out, not_15_out;

  not not_1 (not_1_out, OP_SubOp[4]);
  not not_2 (not_2_out, OP_SubOp[4]);
  not not_3 (not_3_out, OP_SubOp[3]);
  not not_4 (not_4_out, OP_SubOp[2]);
  not not_5 (not_5_out, OP_SubOp[1]);
  not not_6 (not_6_out, OP_SubOp[4]);
  not not_7 (not_7_out, OP_SubOp[3]);
  not not_8 (not_8_out, OP_SubOp[1]);
  not not_9 (not_9_out, OP_SubOp[4]);
  not not_10 (not_10_out, OP_SubOp[3]);
  not not_11 (not_11_out, OP_SubOp[2]);
  not not_12 (not_12_out, OP_SubOp[1]);
  not not_13 (not_13_out, OP_SubOp[3]);
  not not_14 (not_14_out, OP_SubOp[2]);
  not not_15 (not_15_out, OP_SubOp[1]);
  and and_1 (and_1_out, not_2_out, not_3_out, not_4_out, not_5_out);
  and and_2 (and_2_out, not_6_out, not_7_out, OP_SubOp[2], not_8_out);
  and and_3 (and_3_out, not_9_out, not_10_out, OP_SubOp[2], OP_SubOp[1]);
  and and_4 (and_4_out, not_1_out, OP_SubOp[3], not_11_out, not_12_out);
  and and_5 (and_5_out, OP_SubOp[4], not_13_out, not_14_out, not_15_out);
  or or_1 (ALUtru, and_1_out, and_2_out, and_3_out, and_4_out, and_5_out);
endmodule

module PutControl (
  input  SubOp,
  input  [3:0] Opcode,
  output Put
);

  wire not_1_out, not_2_out;

  not not_1 (not_1_out, Opcode[2]);
  not not_2 (not_2_out, SubOp);
  and and_1 (Put, Opcode[3], not_1_out, Opcode[1], Opcode[0], not_2_out);
endmodule

module SwControl (
  input  [3:0] Opcode,
  input  in_2,
  output ALUSrc
);

  wire not_1_out, not_2_out;

  not not_1 (not_1_out, Opcode[3]);
  not not_2 (not_2_out, in_2);
  and and_1 (ALUSrc, Opcode[2], Opcode[1], Opcode[0], not_2_out);
endmodule

module Field (
  input  [15:0] InputData,
  output SubOp,
  output [7:0] Immediate,
  output [2:0] RS,
  output [2:0] RT,
  output [3:0] OpCode
);


  assign Immediate = InputData[8:1];
  assign OpCode = InputData[15:12];
  assign RS = InputData[11:9];
  assign RT = InputData[8:6];
  assign SubOp = InputData[0];
endmodule

module Register2 (
  input  [15:0] WriteInput1,
  input  [15:0] WriteInput2,
  input  WriteEnable1,
  input  WriteEnable2,
  input  Clear,
  input  [2:0] ReadReg,
  input  [2:0] ReadReg2,
  input  Clock,
  output [15:0] Output,
  output [15:0] Output2
);

  wire demultiplexer_3_out0, demultiplexer_3_out1, demultiplexer_3_out2, demultiplexer_3_out3,
       demultiplexer_3_out4, demultiplexer_3_out5, demultiplexer_3_out6, demultiplexer_3_out7,
       demultiplexer_4_out0, demultiplexer_4_out1, demultiplexer_4_out2, demultiplexer_4_out3,
       demultiplexer_4_out4, demultiplexer_4_out5, demultiplexer_4_out6, demultiplexer_4_out7, EnableReg0,
       EnableReg1, EnableReg2, EnableReg3, EnableReg4, EnableReg5, EnableReg6, EnableReg7;
  wire [2:0] WriteReg2;
  wire [15:0] DataReg0, DataReg1, DataReg2, DataReg3, DataReg4, DataReg5, DataReg6, DataReg7,
       demultiplexer_1_out0, demultiplexer_1_out1, demultiplexer_1_out2, demultiplexer_1_out3,
       demultiplexer_1_out4, demultiplexer_1_out5, demultiplexer_1_out6, demultiplexer_1_out7,
       demultiplexer_2_out0, demultiplexer_2_out1, demultiplexer_2_out2, demultiplexer_2_out3,
       demultiplexer_2_out4, demultiplexer_2_out5, demultiplexer_2_out6, demultiplexer_2_out7, r0_q, r1_q,
       r2_q, r3_q, r4_q, r5_q, r6_q, r7_q;

  Demultiplexer #(.select(3), .width(16), .enable("false")) demultiplexer_1 (
    .out0(demultiplexer_1_out0), .out1(demultiplexer_1_out1), .out2(demultiplexer_1_out2),
    .out3(demultiplexer_1_out3), .out4(demultiplexer_1_out4), .out5(demultiplexer_1_out5),
    .out6(demultiplexer_1_out6), .out7(demultiplexer_1_out7), .in(WriteInput1), .sel(ReadReg));
  Demultiplexer #(.select(3), .width(16), .enable("false")) demultiplexer_2 (
    .out0(demultiplexer_2_out0), .out1(demultiplexer_2_out1), .out2(demultiplexer_2_out2),
    .out3(demultiplexer_2_out3), .out4(demultiplexer_2_out4), .out5(demultiplexer_2_out5),
    .out6(demultiplexer_2_out6), .out7(demultiplexer_2_out7), .in(WriteInput2), .sel(WriteReg2));
  Demultiplexer #(.select(3), .enable("false")) demultiplexer_3 (
    .out0(demultiplexer_3_out0), .out1(demultiplexer_3_out1), .out2(demultiplexer_3_out2),
    .out3(demultiplexer_3_out3), .out4(demultiplexer_3_out4), .out5(demultiplexer_3_out5),
    .out6(demultiplexer_3_out6), .out7(demultiplexer_3_out7), .in(WriteEnable1), .sel(ReadReg));
  Demultiplexer #(.select(3), .enable("false")) demultiplexer_4 (
    .out0(demultiplexer_4_out0), .out1(demultiplexer_4_out1), .out2(demultiplexer_4_out2),
    .out3(demultiplexer_4_out3), .out4(demultiplexer_4_out4), .out5(demultiplexer_4_out5),
    .out6(demultiplexer_4_out6), .out7(demultiplexer_4_out7), .in(WriteEnable2), .sel(WriteReg2));
  assign DataReg0 = demultiplexer_1_out0 | demultiplexer_2_out0;  // OR_Gate or_1, 16 bits wide
  assign DataReg1 = demultiplexer_1_out1 | demultiplexer_2_out1;  // OR_Gate or_2, 16 bits wide
  assign DataReg2 = demultiplexer_1_out2 | demultiplexer_2_out2;  // OR_Gate or_3, 16 bits wide
  assign DataReg3 = demultiplexer_1_out3 | demultiplexer_2_out3;  // OR_Gate or_4, 16 bits wide
  assign DataReg4 = demultiplexer_1_out4 | demultiplexer_2_out4;  // OR_Gate or_5, 16 bits wide
  assign DataReg5 = demultiplexer_1_out5 | demultiplexer_2_out5;  // OR_Gate or_6, 16 bits wide
  assign DataReg6 = demultiplexer_1_out6 | demultiplexer_2_out6;  // OR_Gate or_7, 16 bits wide
  assign DataReg7 = demultiplexer_1_out7 | demultiplexer_2_out7;  // OR_Gate or_8, 16 bits wide
  or or_9 (EnableReg1, demultiplexer_3_out1, demultiplexer_4_out1);
  or or_10 (EnableReg2, demultiplexer_3_out2, demultiplexer_4_out2);
  or or_11 (EnableReg3, demultiplexer_3_out3, demultiplexer_4_out3);
  or or_12 (EnableReg4, demultiplexer_3_out4, demultiplexer_4_out4);
  or or_13 (EnableReg5, demultiplexer_3_out5, demultiplexer_4_out5);
  or or_14 (EnableReg6, demultiplexer_3_out6, demultiplexer_4_out6);
  or or_15 (EnableReg7, demultiplexer_3_out7, demultiplexer_4_out7);
  or or_16 (EnableReg0, demultiplexer_3_out0, demultiplexer_4_out0);
  Adder #(.width(3)) adder_1 (.a(3'b111), .b(ReadReg), .out(WriteReg2));  // open: cin, cout
  Register #(.width(16)) r0 (.D(DataReg0), .en(EnableReg0), .Q(r0_q), .clk(Clock), .clr(Clear));
  Register #(.width(16)) r1 (.D(DataReg1), .en(EnableReg1), .Q(r1_q), .clk(Clock), .clr(Clear));
  Register #(.width(16)) r2 (.D(DataReg2), .en(EnableReg2), .Q(r2_q), .clk(Clock), .clr(Clear));
  Register #(.width(16)) r3 (.D(DataReg3), .en(EnableReg3), .Q(r3_q), .clk(Clock), .clr(Clear));
  Register #(.width(16)) r4 (.D(DataReg4), .en(EnableReg4), .Q(r4_q), .clk(Clock), .clr(Clear));
  Register #(.width(16)) r5 (.D(DataReg5), .en(EnableReg5), .Q(r5_q), .clk(Clock), .clr(Clear));
  Register #(.width(16)) r6 (.D(DataReg6), .en(EnableReg6), .Q(r6_q), .clk(Clock), .clr(Clear));
  Register #(.width(16)) r7 (.D(DataReg7), .en(EnableReg7), .Q(r7_q), .clk(Clock), .clr(Clear));
  Multiplexer #(.select(3), .width(16), .enable("false")) multiplexer_1 (
    .in0(r0_q), .in1(r1_q), .in2(r2_q), .in3(r3_q), .in4(r4_q), .in5(r5_q), .in6(r6_q), .in7(r7_q),
    .out(Output), .sel(ReadReg));
  Multiplexer #(.select(3), .width(16), .enable("false")) multiplexer_2 (
    .in0(r0_q), .in1(r1_q), .in2(r2_q), .in3(r3_q), .in4(r4_q), .in5(r5_q), .in6(r6_q), .in7(r7_q),
    .out(Output2), .sel(ReadReg2));

  // Other names for the same wires on the sheet: WriteReg1[2:0] = ReadReg
endmodule

module ALUDecoder (
  input  [3:0] Opcode,
  input  Subop,
  output [2:0] Operation
);

  wire and_1_out, and_2_out, and_3_out, and_4_out, and_5_out, not_1_out, not_2_out, not_3_out;

  and and_1 (and_1_out, Opcode[1], Opcode[0]);
  not not_1 (not_1_out, Opcode[1]);
  and and_2 (and_2_out, not_1_out, Opcode[0]);
  and and_3 (and_3_out, Opcode[1], not_2_out);
  not not_2 (not_2_out, Opcode[0]);
  not not_3 (not_3_out, Opcode[0]);
  and and_4 (and_4_out, not_3_out, Subop);
  and and_5 (and_5_out, Opcode[1], Subop);
  or or_1 (Operation[0], and_1_out, Opcode[2]);
  or or_2 (Operation[1], and_2_out, and_3_out, Opcode[2]);
  or or_3 (Operation[2], and_4_out, and_5_out);
endmodule

module WriteDecoder (
  input  [3:0] Opcode,
  input  Subop,
  output WriteEnable1,
  output WriteEnable2
);

  wire and_1_out, and_2_out, and_3_out, and_4_out, and_5_out, not_1_out, not_2_out, not_3_out, not_4_out,
       not_5_out, not_6_out, not_7_out, not_8_out, not_9_out, not_10_out, not_11_out, not_12_out, not_13_out,
       not_14_out, not_15_out;

  not not_1 (not_1_out, Opcode[3]);
  not not_2 (not_2_out, Opcode[2]);
  not not_3 (not_3_out, Opcode[3]);
  not not_4 (not_4_out, Opcode[1]);
  not not_5 (not_5_out, Opcode[0]);
  not not_6 (not_6_out, Opcode[2]);
  not not_7 (not_7_out, Opcode[1]);
  not not_8 (not_8_out, Opcode[0]);
  not not_9 (not_9_out, Opcode[2]);
  not not_10 (not_10_out, Opcode[1]);
  not not_11 (not_11_out, Subop);
  not not_12 (not_12_out, Opcode[3]);
  not not_13 (not_13_out, Subop);
  not not_14 (not_14_out, Opcode[3]);
  not not_15 (not_15_out, Opcode[2]);
  and and_1 (and_1_out, not_1_out, not_2_out);
  and and_2 (and_2_out, not_3_out, not_4_out, not_5_out);
  and and_3 (and_3_out, not_6_out, not_7_out, not_8_out);
  and and_4 (and_4_out, not_9_out, not_10_out, not_11_out);
  and and_5 (and_5_out, not_12_out, Opcode[1], Opcode[0], not_13_out);
  and and_6 (WriteEnable2, not_14_out, not_15_out, Opcode[1], Opcode[0]);
  or or_1 (WriteEnable1, and_1_out, and_2_out, and_3_out, and_4_out, and_5_out);
endmodule

module ImmAndJumpControl (
  input  Subop,
  input  [3:0] Opcode,
  output Imm,
  output Jump
);

  wire and_1_out, and_2_out, and_3_out, and_4_out, and_5_out, and_6_out, and_7_out, not_1_out, not_2_out,
       not_3_out, not_4_out, not_5_out, not_6_out, not_7_out, not_8_out, not_9_out, not_10_out, not_11_out,
       not_12_out, not_13_out, not_14_out, not_15_out;

  not not_1 (not_1_out, Opcode[3]);
  not not_2 (not_2_out, Opcode[1]);
  not not_3 (not_3_out, Opcode[3]);
  not not_4 (not_4_out, Opcode[0]);
  not not_5 (not_5_out, Opcode[2]);
  not not_6 (not_6_out, Opcode[1]);
  not not_7 (not_7_out, Subop);
  not not_8 (not_8_out, Opcode[2]);
  not not_9 (not_9_out, Opcode[0]);
  not not_10 (not_10_out, Opcode[2]);
  not not_11 (not_11_out, Opcode[1]);
  not not_12 (not_12_out, Opcode[2]);
  not not_13 (not_13_out, Opcode[1]);
  not not_14 (not_14_out, Opcode[2]);
  not not_15 (not_15_out, Opcode[0]);
  and and_1 (and_1_out, not_1_out, not_2_out, Opcode[0]);
  and and_2 (and_2_out, not_3_out, Opcode[2], Opcode[1], not_4_out);
  and and_3 (and_3_out, Opcode[3], not_5_out, not_6_out, not_7_out);
  and and_4 (and_4_out, Opcode[3], not_8_out, not_9_out);
  and and_5 (and_5_out, Opcode[3], not_10_out, not_11_out, Subop);
  and and_6 (and_6_out, Opcode[3], not_12_out, not_13_out, Opcode[0]);
  and and_7 (and_7_out, Opcode[3], not_14_out, Opcode[1], not_15_out);
  or or_1 (Imm, and_1_out, and_2_out, and_3_out, and_4_out);
  or or_2 (Jump, and_5_out, and_6_out, and_7_out);
endmodule

module MemDecoder (
  input  Subop,
  input  [3:0] Opcode,
  output MemWrite,
  output MemRead,
  output MemToReg
);

  wire not_1_out, not_2_out, not_3_out, not_4_out;

  not not_1 (not_1_out, Opcode[3]);
  not not_2 (not_2_out, Opcode[3]);
  not not_3 (not_3_out, Subop);
  not not_4 (not_4_out, Opcode[3]);
  and and_1 (MemWrite, not_1_out, Opcode[2], Opcode[1], Opcode[0], Subop);
  and and_2 (MemRead, not_2_out, Opcode[2], Opcode[1], Opcode[0], not_3_out);
  and and_3 (MemToReg, not_4_out, Opcode[2], Opcode[1], Opcode[0]);
endmodule

module Jr_Jal_Control (
  input  Subop,
  input  [3:0] Opcode,
  output Jr,
  output Jal
);

  wire not_1_out, not_2_out, not_3_out, not_4_out, not_5_out;

  not not_1 (not_1_out, Opcode[2]);
  not not_2 (not_2_out, Opcode[1]);
  not not_3 (not_3_out, Opcode[2]);
  not not_4 (not_4_out, Opcode[1]);
  not not_5 (not_5_out, Subop);
  and and_1 (Jr, Opcode[3], not_1_out, not_2_out, Opcode[0], Subop);
  and and_2 (Jal, Opcode[3], not_3_out, not_4_out, Opcode[0], not_5_out);
endmodule

module ALUControl2 (
  input  Subop,
  input  [3:0] Opcode,
  output [2:0] Operation
);

  wire and_1_out, and_2_out, and_3_out, and_4_out, and_5_out, not_1_out, not_2_out, not_3_out;

  and and_1 (and_1_out, Opcode[1], Opcode[0]);
  not not_1 (not_1_out, Opcode[1]);
  not not_2 (not_2_out, Opcode[0]);
  not not_3 (not_3_out, Opcode[0]);
  or or_1 (Operation[2], and_1_out, Opcode[2], Opcode[3]);
  and and_2 (and_2_out, not_1_out, Opcode[0]);
  and and_3 (and_3_out, Opcode[1], not_2_out);
  and and_4 (and_4_out, not_3_out, Subop);
  and and_5 (and_5_out, Opcode[1], Subop);
  or or_2 (Operation[1], and_2_out, and_3_out, Opcode[2]);
  or or_3 (Operation[0], and_4_out, and_5_out);
endmodule

module AdduiControl (
  input  Subop,
  input  [3:0] Opcode,
  output addui
);

  wire not_1_out, not_2_out, not_3_out;

  not not_1 (not_1_out, Opcode[3]);
  not not_2 (not_2_out, Opcode[2]);
  not not_3 (not_3_out, Opcode[1]);
  and and_1 (addui, not_1_out, not_2_out, not_3_out, Opcode[0], Subop);
endmodule

module Branch (
  input  [3:0] Opcode,
  output b
);

  wire and_1_out, and_2_out, not_1_out, not_2_out, not_3_out, not_4_out;

  not not_1 (not_1_out, Opcode[3]);
  not not_2 (not_2_out, Opcode[1]);
  not not_3 (not_3_out, Opcode[3]);
  not not_4 (not_4_out, Opcode[0]);
  and and_1 (and_1_out, not_1_out, Opcode[2], not_2_out, Opcode[0]);
  or or_1 (b, and_1_out, and_2_out);
  and and_2 (and_2_out, not_3_out, Opcode[2], Opcode[1], not_4_out);
endmodule

module AddiControl (
  input  SubOp,
  input  [3:0] Opcode,
  output addi
);

  wire not_1_out, not_2_out, not_3_out, not_4_out;

  not not_1 (not_1_out, Opcode[3]);
  not not_2 (not_2_out, Opcode[2]);
  not not_3 (not_3_out, Opcode[1]);
  not not_4 (not_4_out, SubOp);
  and and_1 (addi, not_1_out, not_2_out, not_3_out, Opcode[0], not_4_out);
endmodule
