// Logisim project lab11partc-gjh32.circ as structural Verilog: 4 circuits, main circuit main
module main (
  input  in_1,
  input  in_2,
  output out_3
);

  wire _1_out, currentstate_1_newstate_0, currentstate_1_newstate_1, multiplexer_1_out;

  Button _1 (.out(_1_out));
  Multiplexer multiplexer_1 (.in0(in_1), .in1(in_2), .out(multiplexer_1_out), .sel(_1_out));  // open: en
  Clock clock_1 (.out(multiplexer_1_out));
  CurrentState currentstate_1 (
    .State_1(currentstate_1_newstate_1), .State_0(currentstate_1_newstate_0), .Input(multiplexer_1_out),
    .NewState_1(currentstate_1_newstate_1), .NewState_0(currentstate_1_newstate_0), .Trigger(out_3));
endmodule

module CurrentState (
  input  State_1,
  input  State_0,
  input  Input,
  output NewState_1,
  output NewState_0,
  output Trigger
);

  wire and_1_out, not_1_out;

  and and_1 (and_1_out, State_1, State_0);
  not not_1 (not_1_out, Input);
  and and_2 (Trigger, and_1_out, not_1_out);

  assign NewState_0 = Input;
  assign NewState_1 = State_0;
endmodule

module Decoder2 (
  input  A,
  input  B,
  input  C,
  input  D,
  input  SubOP,
  output bp,
  output bn,
  output lw,
  output sw,
  output li,
  output jal,
  output jr,
  output j,
  output put,
  output halt
);

  wire not_1_out, not_2_out, not_3_out, not_4_out, not_5_out, not_6_out, not_7_out, not_8_out, not_9_out,
       not_10_out, not_11_out, not_12_out, not_13_out, not_14_out, not_15_out, not_16_out, not_17_out,
       not_18_out, not_19_out, not_20_out, not_21_out;

  not not_1 (not_1_out, A);
  not not_2 (not_2_out, D);
  not not_3 (not_3_out, SubOP);
  not not_4 (not_4_out, A);
  not not_5 (not_5_out, D);
  not not_6 (not_6_out, A);
  not not_7 (not_7_out, SubOP);
  not not_8 (not_8_out, A);
  not not_9 (not_9_out, B);
  not not_10 (not_10_out, C);
  not not_11 (not_11_out, D);
  not not_12 (not_12_out, B);
  not not_13 (not_13_out, C);
  not not_14 (not_14_out, SubOP);
  not not_15 (not_15_out, B);
  not not_16 (not_16_out, C);
  not not_17 (not_17_out, B);
  not not_18 (not_18_out, D);
  not not_19 (not_19_out, B);
  not not_20 (not_20_out, SubOP);
  not not_21 (not_21_out, B);
  and and_1 (bp, not_1_out, B, C, not_2_out, not_3_out);
  and and_2 (bn, not_4_out, B, C, not_5_out, SubOP);
  and and_3 (lw, not_6_out, B, C, D, not_7_out);
  and and_4 (sw, not_8_out, B, C, D, SubOP);
  and and_5 (li, A, not_9_out, not_10_out, not_11_out);
  and and_6 (jal, A, not_12_out, not_13_out, D, not_14_out);
  and and_7 (jr, A, not_15_out, not_16_out, D, SubOP);
  and and_8 (j, A, not_17_out, C, not_18_out);
  and and_9 (put, A, not_19_out, C, D, not_20_out);
  and and_10 (halt, A, not_21_out, C, D, SubOP);
endmodule

module Decoder1 (
  input  A,
  input  B,
  input  C,
  input  D,
  input  SubOP,
  output \and ,
  output \nor ,
  output addi,
  output addui,
  output add,
  output sub,
  output div,
  output mul,
  output sllv,
  output srlv,
  output bx,
  output bz
);

  wire not_1_out, not_2_out, not_3_out, not_4_out, not_5_out, not_6_out, not_7_out, not_8_out, not_9_out,
       not_10_out, not_11_out, not_12_out, not_13_out, not_14_out, not_15_out, not_16_out, not_17_out,
       not_18_out, not_19_out, not_20_out, not_21_out, not_22_out, not_23_out, not_24_out, not_25_out,
       not_26_out, not_27_out, not_28_out, not_29_out, not_30_out, not_31_out, not_32_out, not_33_out,
       not_34_out, not_35_out, not_36_out, not_37_out, not_38_out, not_39_out, not_40_out;

  not not_1 (not_1_out, A);
  not not_2 (not_2_out, B);
  not not_3 (not_3_out, C);
  not not_4 (not_4_out, D);
  not not_5 (not_5_out, SubOP);
  not not_6 (not_6_out, A);
  not not_7 (not_7_out, B);
  not not_8 (not_8_out, C);
  not not_9 (not_9_out, D);
  not not_10 (not_10_out, A);
  not not_11 (not_11_out, B);
  not not_12 (not_12_out, C);
  not not_13 (not_13_out, SubOP);
  not not_14 (not_14_out, A);
  not not_15 (not_15_out, B);
  not not_16 (not_16_out, C);
  not not_17 (not_17_out, A);
  not not_18 (not_18_out, B);
  not not_19 (not_19_out, D);
  not not_20 (not_20_out, SubOP);
  not not_21 (not_21_out, A);
  not not_22 (not_22_out, B);
  not not_23 (not_23_out, D);
  not not_24 (not_24_out, A);
  not not_25 (not_25_out, B);
  not not_26 (not_26_out, SubOP);
  not not_27 (not_27_out, A);
  not not_28 (not_28_out, B);
  not not_29 (not_29_out, A);
  not not_30 (not_30_out, C);
  not not_31 (not_31_out, D);
  not not_32 (not_32_out, SubOP);
  not not_33 (not_33_out, A);
  not not_34 (not_34_out, C);
  not not_35 (not_35_out, D);
  not not_36 (not_36_out, A);
  not not_37 (not_37_out, C);
  not not_38 (not_38_out, SubOP);
  not not_39 (not_39_out, A);
  not not_40 (not_40_out, C);
  and and_1 (\and , not_1_out, not_2_out, not_3_out, not_4_out, not_5_out);
  and and_2 (\nor , not_6_out, not_7_out, not_8_out, not_9_out, SubOP);
  and and_3 (addi, not_10_out, not_11_out, not_12_out, D, not_13_out);
  and and_4 (addui, not_14_out, not_15_out, not_16_out, D, SubOP);
  and and_5 (add, not_17_out, not_18_out, C, not_19_out, not_20_out);
  and and_6 (sub, not_21_out, not_22_out, C, not_23_out, SubOP);
  and and_7 (div, not_24_out, not_25_out, C, D, not_26_out);
  and and_8 (mul, not_27_out, not_28_out, C, D, SubOP);
  and and_9 (sllv, not_29_out, B, not_30_out, not_31_out, not_32_out);
  and and_10 (srlv, not_33_out, B, not_34_out, not_35_out, SubOP);
  and and_11 (bx, not_36_out, B, not_37_out, D, not_38_out);
  and and_12 (bz, not_39_out, B, not_40_out, D, SubOP);
endmodule
