// Logisim project adder.circ as structural Verilog: 1 circuit, main circuit main
module main (
  input  Carryin,
  input  A,
  input  B,
  output Sum,
  output CarryOut
);

  wire and_1_out, and_2_out, and_3_out, and_4_out, and_5_out, and_6_out, and_7_out, not_1_out, not_2_out,
       not_3_out;

  not not_1 (not_1_out, Carryin);
  not not_2 (not_2_out, A);
  not not_3 (not_3_out, A);
  and and_1 (and_1_out, not_2_out, not_3_out, Carryin);
  and and_2 (and_2_out, not_2_out, A, not_1_out);
  and and_3 (and_3_out, A, not_3_out, not_1_out);
  and and_4 (and_4_out, A, A, Carryin);
  and and_5 (and_5_out, A, Carryin);
  and and_6 (and_6_out, A, Carryin);
  and and_7 (and_7_out, A, A);
  or or_1 (Sum, and_1_out, and_4_out, and_2_out, and_3_out);
  or or_2 (CarryOut, and_5_out, and_6_out, and_7_out);

  assign B = A;
endmodule
