// Logisim project jrmipsproject.circ as structural Verilog
module ALU (
  input  [15:0] Input_1,
  input  [15:0] Input_2,
  input  [1:0] in_3,
  output [15:0] ALU_Output
);

  wire [15:0] adder_1_out, and_1_out, nor_1_out, subtractor_1_out;

  assign and_1_out = Input_1 & Input_2;  // AND_Gate and_1, 16 bits wide
  assign nor_1_out = ~(Input_1 | Input_2);  // NOR_Gate nor_1, 16 bits wide
  Adder #(.width(16)) adder_1 (.a(Input_1), .b(Input_2), .out(adder_1_out));  // open: cin, cout
  Subtractor #(.width(16)) subtractor_1 (.a(Input_1), .b(Input_2), .out(subtractor_1_out));  // open: bin, bout
  Multiplexer #(.select(2), .width(16)) multiplexer_1 (
    .in0(and_1_out), .in1(nor_1_out), .in2(adder_1_out), .in3(subtractor_1_out), .out(ALU_Output), .sel(in_3));  // open: en

  // Notes on the sheet:
  //   ALU- Graham Hoehing
endmodule

module Register_File (
  input  Write_Enable,
  input  [2:0] WriteRegister,
  input  [15:0] Write_Data,
  input  [2:0] ReadRegister1,
  input  [2:0] ReadRegister2,
  input  Clock,
  output [15:0] Read_Data1,
  output [15:0] Read_Data2
);

  wire demultiplexer_2_out0, demultiplexer_2_out1, demultiplexer_2_out2, demultiplexer_2_out3,
       demultiplexer_2_out4, demultiplexer_2_out5, demultiplexer_2_out6, demultiplexer_2_out7, undriven;
  wire [15:0] demultiplexer_1_out0, demultiplexer_1_out1, demultiplexer_1_out2, demultiplexer_1_out3,
       demultiplexer_1_out4, demultiplexer_1_out5, demultiplexer_1_out7, register_1_q, register_2_q,
       register_3_q, register_4_q, register_5_q, register_6_q, register_7_q, register_8_q;

  Demultiplexer #(.select(3), .width(16)) demultiplexer_1 (
    .out0(demultiplexer_1_out0), .out1(demultiplexer_1_out1), .out2(demultiplexer_1_out2),
    .out3(demultiplexer_1_out3), .out4(demultiplexer_1_out4), .out5(demultiplexer_1_out5),
    .out6(demultiplexer_1_out0), .out7(demultiplexer_1_out7), .in(Write_Data), .sel(WriteRegister));  // open: en
  Demultiplexer #(.select(3)) demultiplexer_2 (
    .out0(demultiplexer_2_out0), .out1(demultiplexer_2_out1), .out2(demultiplexer_2_out2),
    .out3(demultiplexer_2_out3), .out4(demultiplexer_2_out4), .out5(demultiplexer_2_out5),
    .out6(demultiplexer_2_out6), .out7(demultiplexer_2_out7), .in(Write_Enable), .sel(WriteRegister));  // open: en
  Register #(.width(16)) register_1 (
    .D(demultiplexer_1_out3), .en(demultiplexer_2_out3), .Q(register_1_q), .clk(Clock));  // open: clr
  Register #(.width(16)) register_2 (
    .D(demultiplexer_1_out0), .en(demultiplexer_2_out0), .Q(register_2_q), .clk(Clock));  // open: clr
  Register #(.width(16)) register_3 (
    .D(demultiplexer_1_out1), .en(demultiplexer_2_out1), .Q(register_3_q), .clk(Clock));  // open: clr
  Register #(.width(16)) register_4 (
    .D(demultiplexer_1_out2), .en(demultiplexer_2_out2), .Q(register_4_q), .clk(Clock));  // open: clr
  Register #(.width(16)) register_5 (
    .D(demultiplexer_1_out4), .en(demultiplexer_2_out4), .Q(register_5_q), .clk(Clock));  // open: clr
  Register #(.width(16)) register_6 (
    .D(demultiplexer_1_out5), .en(demultiplexer_2_out5), .Q(register_6_q), .clk(Clock));  // open: clr
  Register #(.width(16)) register_7 (
    .D(demultiplexer_1_out0), .en(demultiplexer_2_out6), .Q(register_7_q), .clk(Clock));  // open: clr
  Register #(.width(16)) register_8 (
    .D(demultiplexer_1_out7), .en(demultiplexer_2_out7), .Q(register_8_q), .clk(Clock));  // open: clr
  Multiplexer #(.select(3), .width(16)) multiplexer_1 (
    .in0(register_2_q), .in1(register_3_q), .in2(register_4_q), .in3(register_1_q), .in4(register_5_q),
    .in5(register_6_q), .in6(register_7_q), .in7(register_8_q), .out(Read_Data1), .sel(ReadRegister1),
    .en(undriven));
  Multiplexer #(.select(3), .width(16)) multiplexer_2 (
    .in0(register_2_q), .in1(register_3_q), .in2(register_4_q), .in3(register_1_q), .in4(register_5_q),
    .in5(register_6_q), .in6(register_7_q), .in7(register_8_q), .out(Read_Data2), .sel(ReadRegister2));  // open: en

  // Other names for the same wires on the sheet: A[2:0] = ReadRegister1; B[2:0] = ReadRegister2
endmodule
