// Logisim project lab08part3-gjh32.circ as structural Verilog: 1 circuit, main circuit main
module main (
  input  A,
  input  B,
  input  C,
  output V
);

  wire A1_out, A2_out, A3_out, not_1_out;

  not not_1 (not_1_out, A);
  not not_2 (not_1_out, B);
  not not_3 (not_1_out, C);
  and A1 (A1_out, not_1_out, not_1_out);
  and A2 (A2_out, not_1_out, not_1_out);
  and A3 (A3_out, not_1_out, not_1_out);
  or O1 (V, A1_out, A2_out, A3_out);
endmodule
